// Logisim project 实验一 多数决.circ as structural Verilog: 2 circuits, main circuit L_6f90e275
// Bool
module L_6f90e275 (
  input  A,
  input  B,
  input  C,
  output F
);

  wire and_1_out, and_2_out, and_3_out, and_4_out, and_5_out, and_6_out, nand_1_out, nand_2_out, nand_3_out,
       nand_4_out;

  and and_1 (and_1_out, A, B);
  and and_2 (and_2_out, A, B);
  and and_3 (and_3_out, ~B, A);  // AND_Gate
  and and_4 (and_4_out, ~A, B);  // AND_Gate
  nand nand_1 (nand_1_out, and_1_out, C);
  nand nand_2 (nand_2_out, ~C, and_2_out);  // NAND_Gate
  nand nand_3 (nand_3_out, and_3_out, C);
  nand nand_4 (nand_4_out, and_4_out, C);
  and and_5 (and_5_out, nand_1_out, nand_2_out);
  nand nand_5 (F, and_5_out, and_6_out);
  and and_6 (and_6_out, nand_3_out, nand_4_out);
endmodule

// sTruth
module L_68fb15ca (
  input  X1,
  input  X0,
  input  Y1,
  input  Y0,
  output Gt
);


  // Notes on the sheet:
  //   输入引脚
  //   请勿增加、删除引脚，用隧道标签构建电路
  //   请勿更改电路封装外观
  //   输出引脚
endmodule
