// Logisim project 实验一 奇偶校验.circ as structural Verilog: 1 circuit, main circuit main
module main (
  input  in_1,
  input  in_2,
  input  in_3,
  input  in_4,
  output out_5
);

  wire and_1_out, and_2_out, and_3_out, and_4_out, and_5_out, and_6_out, and_7_out, and_8_out, and_9_out,
       and_10_out, and_11_out, and_12_out, and_13_out, and_14_out, and_15_out, and_16_out, and_17_out,
       and_18_out, and_19_out, and_20_out, and_21_out, and_22_out, nand_1_out, nand_2_out, nand_3_out,
       nand_4_out, nand_5_out, nand_6_out, nand_7_out, nand_8_out;

  and and_1 (and_1_out, ~in_1, in_2);  // AND_Gate
  and and_2 (and_2_out, in_1, ~in_2);  // AND_Gate
  and and_3 (and_3_out, in_1, in_2);
  and and_4 (and_4_out, in_1, in_2);
  and and_5 (and_5_out, in_1, ~in_2);  // AND_Gate
  and and_6 (and_6_out, ~in_1, in_2);  // AND_Gate
  and and_7 (and_7_out, ~in_1, ~in_2);  // AND_Gate
  and and_8 (and_8_out, ~in_1, ~in_2);  // AND_Gate
  and and_9 (and_9_out, and_1_out, in_3);
  and and_10 (and_10_out, and_2_out, in_3);
  and and_11 (and_11_out, and_3_out, ~in_3);  // AND_Gate
  and and_12 (and_12_out, and_4_out, in_3);
  and and_13 (and_13_out, and_5_out, ~in_3);  // AND_Gate
  and and_14 (and_14_out, and_6_out, ~in_3);  // AND_Gate
  and and_15 (and_15_out, and_7_out, in_3);
  and and_16 (and_16_out, and_8_out, ~in_3);  // AND_Gate
  nand nand_1 (nand_1_out, and_9_out, in_4);
  nand nand_2 (nand_2_out, and_10_out, in_4);
  nand nand_3 (nand_3_out, and_11_out, in_4);
  nand nand_4 (nand_4_out, and_12_out, ~in_4);  // NAND_Gate
  nand nand_5 (nand_5_out, and_13_out, ~in_4);  // NAND_Gate
  nand nand_6 (nand_6_out, and_14_out, ~in_4);  // NAND_Gate
  nand nand_7 (nand_7_out, and_15_out, ~in_4);  // NAND_Gate
  nand nand_8 (nand_8_out, and_16_out, in_4);
  and and_17 (and_17_out, nand_1_out, nand_2_out);
  and and_18 (and_18_out, and_17_out, nand_3_out);
  and and_19 (and_19_out, nand_5_out, nand_6_out);
  and and_20 (and_20_out, and_19_out, nand_7_out);
  and and_21 (and_21_out, and_18_out, nand_4_out);
  nand nand_9 (out_5, and_21_out, and_22_out);
  and and_22 (and_22_out, and_20_out, nand_8_out);

  // Notes on the sheet:
  //   请完成四位奇偶校验电路设计，当输入有奇数个1时输出点亮，否则不亮
endmodule
