// Logisim project 实验三 74ls85.circ as structural Verilog: 1 circuit, main circuit main
module main (
  input  A,
  input  in_2,
  input  in_3,
  input  in_4,
  input  in_5,
  input  in_6,
  input  in_7,
  input  in_8,
  input  B,
  input  in_10,
  input  in_11,
  input  in_12,
  input  in_13,
  input  in_14,
  input  in_15,
  input  in_16
);

  wire and_1_out, n7485_1_pin5, n7485_1_pin6, n7485_2_pin5, n7485_2_pin6, or_1_out, or_2_out;

  _7485 #(.ShowInternalStructure("true")) u_7485_1 (
    .pin1(B), .pin5(n7485_1_pin5), .pin6(n7485_1_pin6), .pin15(A), .pin14(in_10), .pin13(in_2), .pin12(in_3),
    .pin11(in_11), .pin10(in_4), .pin9(in_12));  // open: pin2, pin3, pin4, pin7
  or or_1 (or_1_out, n7485_2_pin5, n7485_2_pin6);
  and and_1 (and_1_out, or_1_out, or_2_out);
  LED led_1 (.in(and_1_out));
  or or_2 (or_2_out, n7485_1_pin5, n7485_1_pin6);
  _7485 #(.ShowInternalStructure("true")) u_7485_2 (
    .pin1(in_13), .pin5(n7485_2_pin5), .pin6(n7485_2_pin6), .pin15(in_5), .pin14(in_14), .pin13(in_6),
    .pin12(in_7), .pin11(in_15), .pin10(in_8), .pin9(in_16));  // open: pin2, pin3, pin4, pin7
endmodule
